# Fritzing sketch 433 mHz to Arduino UNO (saved by Fritzing 0.9.3b)

parts:
  Part1 = Arduino Uno (Rev3)
  Part2 = Arduino Uno (Rev3)
  A1 = Hiletgo 315mhz tx [package=THT]
  A2 = Hiletgo 315mhz rx [package=THT]

nets:
  N1: Part1.D12/MISO, A1.pin2
  N2: Part1.5V, A1.pin1
  N3: Part1.GND, A1.pin3
  N4: Part2.D11_PWM/MOSI, A2.pin2
  N5: Part2.5V, A2.pin1
  N6: Part2.GND, A2.pin4

custom parts:
  Hiletgo 315mhz tx: 315Mhz RF Transmitter and Receiver Module link kit, transmitter.
  Hiletgo 315mhz rx: 315Mhz RF Transmitter and Receiver Module link kit, receiver.
