# Fritzing sketch Ultimate GPS to Arduino UNO (saved by Fritzing 0.9.3b)

parts:
  GPS1 = Adafruit Ultimate GPS Breakout
  Part1 = Arduino Uno (Rev3)

nets:
  N1: GPS1.TX, Part1.D8
  N2: GPS1.RX, Part1.D7
  GND: GPS1.GND, Part1.GND
  VIN: GPS1.VIN, Part1.5V
