# Fritzing sketch Untitled Sketch 2 (saved by Fritzing 0.9.10b)

parts:
  Part1 = Arduino Mega 2560 (Rev3)
  A4_-_Adjust_Toggle = Toggle Switch [package=THT]
  A3_-_Adjust_Toggle = Toggle Switch [package=THT]
  A2_-_Adjust_Toggle = Toggle Switch [package=THT]
  A1_-_Adjust_Toggle = Toggle Switch [package=THT]
  U1 = POT [knob_status=50% power=0.5W package=alps_pot]
  U2 = POT [knob_status=50% power=0.5W package=alps_pot]
  U3 = POT [knob_status=50% power=0.5W package=alps_pot]
  U4 = POT [knob_status=50% power=0.5W package=alps_pot]
  Mission_1 = Round Pushbutton
  ESTOP = Square Pushbutton
  Mission_Go_Button = Round Pushbutton
  Mission_4 = Round Pushbutton
  Mission_2 = Round Pushbutton
  Mission_3 = Round Pushbutton
  Move_Backward = Round Pushbutton
  Move_Forward = Round Pushbutton
  Move_Right = Round Pushbutton
  Move_Left = Round Pushbutton
  A1_-_SetSpeed = Round Pushbutton
  A2_-_SetForwardTime = Round Pushbutton
  A3_-_SetTurnSpeed = Round Pushbutton
  A4_-_SetTurnTime = Round Pushbutton
  LED3 = LED - 5mm [color="Red (633nm)" current=0.030 package="5 mm [THT]"]
  LED4 = LED - 5mm [color="Red (633nm)" current=0.030 package="5 mm [THT]"]
  U5 = RF-LINK_TX [package=rf-link_tx]
  U6 = RF-LINK_TX [package=rf-link_tx]

nets:
  N1: Part1.A0, U1.S
  N2: Part1.A1, U2.S
  N3: Part1.A2, U3.S
  N4: Part1.A3, U4.S
  N5: Part1.D21/SCL, LED4.cathode
  N6: Part1.D20/SDA, LED3.cathode
  N7: Part1.D19/RX1, U5.DATA
  N8: Part1.D18/TX1, U6.DATA
  N9: Part1.D17_PWM/RX2, A4_-_SetTurnTime.leg0
  N10: Part1.D16_PWM/TX2, A3_-_SetTurnSpeed.leg0
  N11: Part1.D15/RX3, A2_-_SetForwardTime.leg0
  N12: Part1.D14/TX3, A1_-_SetSpeed.leg0
  GND: Part1.GND, A4_-_Adjust_Toggle.COM, A3_-_Adjust_Toggle.COM, A2_-_Adjust_Toggle.COM, A1_-_Adjust_Toggle.COM, U1.A, U2.A, U3.A, U4.A, Mission_1.leg1, ESTOP.leg0, Mission_4.leg1, Mission_3.leg1, Move_Backward.leg1, Move_Forward.leg1, Move_Right.leg1, Move_Left.leg1, A1_-_SetSpeed.leg1, A2_-_SetForwardTime.leg1, A3_-_SetTurnSpeed.leg1, A4_-_SetTurnTime.leg1, LED3.anode, LED4.anode, U5.GND, U6.GND
  N13: Part1.D12_PWM, Mission_Go_Button.leg0
  N14: Part1.D11_PWM, Mission_1.leg0
  N15: Part1.D10_PWM, Mission_2.leg0
  N16: Part1.D9_PWM, Mission_3.leg0
  N17: Part1.D8_PWM, Mission_4.leg0
  +5V: Part1.5V, U1.E, U2.E, U3.E, U4.E, U5.+5V, U6.+5V
  N18: Part1.D3_PWM, ESTOP.leg1
  N19: Part1.D4_PWM, Move_Forward.leg0
  N20: Part1.D5_PWM, Move_Right.leg0
  N21: Part1.D6_PWM, Move_Left.leg0
  N22: Part1.D7_PWM, Move_Backward.leg0
  N23: Part1.D27, A1_-_Adjust_Toggle.L1
  N24: Part1.D28, A3_-_Adjust_Toggle.L1
  N25: Part1.D29, A2_-_Adjust_Toggle.L1
  N26: Part1.D30, A4_-_Adjust_Toggle.L1
  N27: Mission_Go_Button.leg1, Mission_2.leg1
